// Digital circuit 74LS163A.dig as structural Verilog
module _74LS163A (
  input  CLK,
  input  A,
  input  LD,
  input  CLR,
  input  B,
  input  P,
  input  T,
  input  C,
  input  D,
  output QA,
  output QB,
  output QC,
  output QD,
  output CO
);

  wire and_1_out, and_2_out, and_3_out, and_4_out, and_5_out, and_6_out, and_7_out, and_8_out, and_9_out,
       and_10_out, and_11_out, and_12_out, and_13_out, and_14_out, DA_nq, DB_nq, DC_nq, DD_nq, nand_1_out,
       nand_2_out, nand_3_out, not_1_out, not_2_out, or_1_out, or_2_out, or_3_out, or_4_out, SET;

  not not_1 (not_1_out, CLR);
  and and_1 (and_1_out, ~not_1_out, ~LD);  // And
  and and_2 (and_2_out, LD, CLR, P, T);
  and and_3 (and_3_out, A, and_1_out);
  and and_4 (and_4_out, B, and_1_out);
  and and_5 (and_5_out, C, and_1_out);
  and and_6 (and_6_out, D, and_1_out);
  nor nor_1 (SET, not_1_out, and_1_out);
  nand nand_1 (nand_1_out, QA, and_2_out);
  nand nand_2 (nand_2_out, QA, QB, and_2_out);
  nand nand_3 (nand_3_out, QA, QB, QC, and_2_out);
  not not_2 (not_2_out, and_2_out);
  and and_7 (and_7_out, QA, not_2_out, SET);
  and and_8 (and_8_out, and_2_out, DA_nq);
  and and_9 (and_9_out, QB, nand_1_out, SET);
  and and_10 (and_10_out, QA, and_2_out, DB_nq);
  and and_11 (and_11_out, QC, nand_2_out, SET);
  and and_12 (and_12_out, QA, QB, and_2_out, DC_nq);
  and and_13 (and_13_out, QD, nand_3_out, SET);
  and and_14 (and_14_out, QA, QB, QC, and_2_out, DD_nq);
  and and_15 (CO, QA, QB, QC, QD, T);
  or or_1 (or_1_out, and_7_out, and_8_out, and_3_out);
  or or_2 (or_2_out, and_9_out, and_10_out, and_4_out);
  or or_3 (or_3_out, and_11_out, and_12_out, and_5_out);
  or or_4 (or_4_out, and_13_out, and_14_out, and_6_out);
  D_FF DA (.D(or_1_out), .C(CLK), .Q(QA), .nQ(DA_nq));
  D_FF DB (.D(or_2_out), .C(CLK), .Q(QB), .nQ(DB_nq));
  D_FF DC (.D(or_3_out), .C(CLK), .Q(QC), .nQ(DC_nq));
  D_FF DD (.D(or_4_out), .C(CLK), .Q(QD), .nQ(DD_nq));
  Seven_Seg_Hex seven_seg_hex_1 (.d({QD, QC, QB, QA}), .dp(1'b0));

  // Other names for the same wires on the sheet: AA = QA; BB = QB; CC = QC; DD = QD

  // Notes on the sheet:
  //   LD: default 1
  //   CLR: default 1
  //   P: Enable P
  //   T: Enable T
  //   CO: Ripple carry
  //   Count enable
  //   Active high
  //   Load (internal)
  //   Active high
  //   Low when CLR
  //   or LD is low
endmodule
