// Digital circuit LB_MR5A16.dig as structural Verilog
module LB_MR5A16 (
  input  E,
  input  G,
  input  W,
  input  B,
  input  [21:0] A,
  input  D0,
  input  D1,
  input  D2,
  input  D3,
  input  D4,
  input  D5,
  input  D6,
  input  D7,
  output OE
);

  wire or_1_out;
  wire [7:0] LB_d;

  or or_1 (or_1_out, W, B);
  and and_1 (OE, ~E, W, ~B, ~G);  // And
  RAMSinglePortSel #(.AddrBits(22), .isProgramMemory("true"), .Bits(8)) LB (
    .A(A), .CS(~E), .WE(~or_1_out), .OE(~OE), .D(LB_d));
  BusSplitter #(.Bits(8)) bussplitter_1 (
    .D(LB_d), .OE(OE), .D0(D0), .D1(D1), .D2(D2), .D3(D3), .D4(D4), .D5(D5), .D6(D6), .D7(D7));

  // Notes on the sheet:
  //   E: Chip select
  //   G: Output enable (with UB#, LB#)
  //   W: Write enable
  //   B: Byte write/output enable
  //   A: Address 21:0
  //   D0: Output enable (with UB#, LB#)
  //   D1: Output enable (with UB#, LB#)
  //   D2: Output enable (with UB#, LB#)
  //   D3: Output enable (with UB#, LB#)
  //   D4: Output enable (with UB#, LB#)
  //   D5: Output enable (with UB#, LB#)
  //   D6: Output enable (with UB#, LB#)
  //   D7: Output enable (with UB#, LB#)
  //   OE: Output enable for this byte
  //   The MR5A16 nonvolatile static RAM is 16 bits wide. It has UB# and LB# (upper and lower byte)
  //   inputs to allow byte reads and writes at the selected 22-bit word address (both must be asserted
  //   for a word access). I can partially simulate its nonvolatility using Digital's "Program Memory" feature
  //   with an associated file, but Digital associates one file per subcircuit, not one file per component;
  //   so each 8-bit wide component needs to be in a separate subcircuit, and the two subcircuits need
  //   to be configured for distinct upper- and lower-byte backing files UB-NVRAM and LB-NVRAM.
endmodule
