// Digital circuit MR5A16.dig as structural Verilog
module MR5A16 (
  input  E,
  input  G,
  input  W,
  input  UB,
  input  LB,
  input  [21:0] A,
  input  [7:0] DL,
  input  [7:0] DH
);

  wire bussplitter_1_d0, bussplitter_1_d1, bussplitter_1_d2, bussplitter_1_d3, bussplitter_1_d4,
       bussplitter_1_d5, bussplitter_1_d6, bussplitter_1_d7, bussplitter_2_d0, bussplitter_2_d1,
       bussplitter_2_d2, bussplitter_2_d3, bussplitter_2_d4, bussplitter_2_d5, bussplitter_2_d6,
       bussplitter_2_d7, OEH, OEL;

  BusSplitter #(.Bits(8)) bussplitter_1 (
    .D(DL), .OE(OEL), .D0(bussplitter_1_d0), .D1(bussplitter_1_d1), .D2(bussplitter_1_d2),
    .D3(bussplitter_1_d3), .D4(bussplitter_1_d4), .D5(bussplitter_1_d5), .D6(bussplitter_1_d6),
    .D7(bussplitter_1_d7));
  BusSplitter #(.Bits(8)) bussplitter_2 (
    .D(DH), .OE(OEH), .D0(bussplitter_2_d0), .D1(bussplitter_2_d1), .D2(bussplitter_2_d2),
    .D3(bussplitter_2_d3), .D4(bussplitter_2_d4), .D5(bussplitter_2_d5), .D6(bussplitter_2_d6),
    .D7(bussplitter_2_d7));
  LB_MR5A16 lb_mr5a16_1 (
    .E(E), .G(G), .W(W), .B(LB), .A(A), .D0(bussplitter_1_d0), .D1(bussplitter_1_d1), .D2(bussplitter_1_d2),
    .D3(bussplitter_1_d3), .D4(bussplitter_1_d4), .D5(bussplitter_1_d5), .D6(bussplitter_1_d6),
    .D7(bussplitter_1_d7), .OE(OEL));
  UB_MR5A16 ub_mr5a16_1 (
    .E(E), .G(G), .W(W), .B(UB), .A(A), .D8(bussplitter_2_d0), .D9(bussplitter_2_d1), .D10(bussplitter_2_d2),
    .D11(bussplitter_2_d3), .D12(bussplitter_2_d4), .D13(bussplitter_2_d5), .D14(bussplitter_2_d6),
    .D15(bussplitter_2_d7), .OE(OEH));

  // Notes on the sheet:
  //   E: Chip select, default 1
  //   G: Output enable (with UB#, LB#), default 1
  //   W: Write enable, default 1
  //   UB: Upper byte write/output enable, default 1
  //   LB: Lower byte write/output enable, default 1
  //   A: Address 21:0
endmodule
