// Digital circuit NonOverlappingClock_BAD.dig as structural Verilog
module NonOverlappingClock_BAD (
  input  clk,
  input  clk_2,
  output out_2,
  output out_3
);

  wire delay_1_out, nor_1_out, nor_2_out, nor_3_out, nor_4_out, not_1_out, not_2_out, not_3_out, not_4_out,
       not_7_out, not_8_out, not_9_out, not_10_out;
  wire [2:0] counter_1_out;

  Counter #(.Bits(3)) counter_1 (.en(1'b1), .C(clk_2), .clr(1'b0), .out(counter_1_out));  // open: ovf
  not not_1 (not_1_out, clk);
  not not_2 (not_2_out, counter_1_out[2]);
  nor nor_1 (nor_1_out, not_1_out, out_3);
  nor nor_2 (nor_2_out, out_2, clk);
  nor nor_3 (nor_3_out, delay_1_out, not_10_out);
  Delay #(.delayTime(11)) delay_1 (.in(not_2_out), .out(delay_1_out));
  nor nor_4 (nor_4_out, not_9_out, counter_1_out[2]);
  not not_3 (not_3_out, nor_1_out);
  not not_4 (not_4_out, nor_2_out);
  not not_5 (out_2, not_3_out);
  not not_6 (out_3, not_4_out);
  not not_7 (not_7_out, nor_3_out);
  not not_8 (not_8_out, nor_4_out);
  not not_9 (not_9_out, not_7_out);
  not not_10 (not_10_out, not_8_out);

  // Notes on the sheet:
  //   This doesn't work. There is supposed to be "dead time"
  //   between the output transitions.
endmodule
