// Digital circuit SRLatch.dig as structural Verilog
module SRLatch (
  input  in_1,
  input  in_2,
  output out_3,
  output out_4
);

  nor nor_1 (out_3, in_1, out_4);
  nor nor_2 (out_4, out_3, in_2);

  // Notes on the sheet:
  //   RESET
  //   SET
  //   Q
  //   Q#
endmodule
