// Digital circuit UB_MR5A16.dig as structural Verilog
module UB_MR5A16 (
  input  E,
  input  G,
  input  W,
  input  B,
  input  [21:0] A,
  input  D8,
  input  D9,
  input  D10,
  input  D11,
  input  D12,
  input  D13,
  input  D14,
  input  D15,
  output OE
);

  wire or_1_out;
  wire [7:0] UB_d;

  or or_1 (or_1_out, W, B);
  and and_1 (OE, ~E, W, ~B, ~G);  // And
  RAMSinglePortSel #(.AddrBits(22), .isProgramMemory("true"), .Bits(8)) UB (
    .A(A), .CS(~E), .WE(~or_1_out), .OE(~OE), .D(UB_d));
  BusSplitter #(.Bits(8)) bussplitter_1 (
    .D(UB_d), .OE(OE), .D0(D8), .D1(D9), .D2(D10), .D3(D11), .D4(D12), .D5(D13), .D6(D14), .D7(D15));

  // Notes on the sheet:
  //   E: Chip select
  //   G: Output enable (with UB#, LB#)
  //   W: Write enable
  //   B: Byte write/output enable
  //   A: Address 21:0
  //   D8: Output enable (with UB#, LB#)
  //   D9: Output enable (with UB#, LB#)
  //   D10: Output enable (with UB#, LB#)
  //   D11: Output enable (with UB#, LB#)
  //   D12: Output enable (with UB#, LB#)
  //   D13: Output enable (with UB#, LB#)
  //   D14: Output enable (with UB#, LB#)
  //   D15: Output enable (with UB#, LB#)
  //   OE: Output enable for this byte
  //   The MR5A16 nonvolatile static RAM is 16 bits wide. It has UB# and LB# (upper and lower byte)
  //   inputs to allow byte reads and writes at the selected 22-bit word address (both must be asserted
  //   for a word access). I can partially simulate its nonvolatility using Digital's "Program Memory" feature
  //   with an associated file, but Digital associates one file per subcircuit, not one file per component;
  //   so each 8-bit wide component needs to be in a separate subcircuit, and the two subcircuits need
  //   to be configured for distinct upper- and lower-byte backing files UB-NVRAM and LB-NVRAM.
endmodule
